# Fritzing sketch Перевозчик (saved by Fritzing 0.9.3b)

parts:
  Часть2 = Adafruit Motor/Stepper/Servo Shield [part_number="Adafruit #1438"]
  Часть3 = Adafruit TCS34725 RGB Color Sensor [part_number="Adafruit #1334"]
  Часть1 = Arduino Mega 2560 (Rev3)
  U4 = ENCODER-QUADRATURE [package=encoder-16mm-quad]
  M5 = DC Motor
  M6 = DC Motor
  J1 = Basic Servo
  U5 = LIPO-110mAh [package=lipo-110]
  U6 = SWITCH-SPST-2 [package=switch-spst-vertical]
  J2 = Infrared Proximity Sensor  # not connected
  M7 = DC Motor  # not connected
  U7 = ENCODER-QUADRATURE [package=encoder-16mm-quad]
  LED1 = RGB LED (com. cathode, rgb) [package="5 mm [THT]"]

nets:
  N1: Часть2.M2A, M6.pin_1
  N2: Часть2.M1B, M5.pin_1
  N3: Часть2.M1A, M5.pin_2
  N4: Часть2.GND, U5.-
  N5: Часть2.VMOTOR, U6.O
  N6: Часть2.N$38, J1.pulse
  VIN: Часть3.VIN, Часть1.5V
  GND: Часть3.GND, Часть1.GND
  N7: Часть3.SCL, Часть1.D21/SCL
  N8: Часть3.SDA, Часть1.D20/SDA
  N9: Часть1.D19/RX1, U4.C
  N10: Часть1.D39, LED1.red_anode
  N11: Часть1.D41, LED1.common_cathode
  N12: Часть1.D43, LED1.green_anode
  N13: U4.A, U7.A
  N14: U4.B, U7.B
  N15: U5.+, U6.P

custom parts:
  Adafruit Motor/Stepper/Servo Shield: The original Adafruit Motorshield kit is one of our most beloved kits, which is why we decided to make something even better. We have upgraded the shield kit to make the bestest, easiest way to drive DC and Stepper motors. This shield will make quick work of your next robotics project! We kept the ability to drive up to 4 DC motors or 2 stepper motors, but added many improvements: Instead of a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
  Adafruit TCS34725 RGB Color Sensor: Your electronics can now see in dazzling color with this lovely color light sensor. We found the best color sensor on the market, the TCS34725, which has RGB and Clear light sensing elements. An IR blocking filter, integrated on-chip and localized to the color sensing photodiodes, minimizes the IR spectral component of the incoming light and allows color measurements to be made accurately. The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
